# Fritzing sketch ESP32_Nokia511 (saved by Fritzing 0.9.3b)
breadboards: 1

parts:
  Nokia_5110_LCD_Module1 = Nokia 5110 LCD
  A1 = ESP32 DOIT DEVKIT V1 36pin
  R1 = Resistor [tolerance=±5% resistance=10k package=THT]

nets:
  N1: Nokia_5110_LCD_Module1.VCC, A1.Pin_22
  N2: Nokia_5110_LCD_Module1.GND, A1.Pin_26
  N3: Nokia_5110_LCD_Module1.SCE, A1.Pin_23
  N4: Nokia_5110_LCD_Module1.RST, A1.Pin_36
  N5: Nokia_5110_LCD_Module1.D/C, A1.Pin_27
  N6: Nokia_5110_LCD_Module1.DN(MOSI), A1.Pin_19
  N7: Nokia_5110_LCD_Module1.SCLK, R1.Pin_0
  N8: Nokia_5110_LCD_Module1.LED, A1.Pin_20
  N9: A1.Pin_18, R1.Pin_1

custom parts:
  Nokia 5110 LCD: Nokia 5110 Graphic 84*48 LCD module such as the Sparkfun LCD-10168 or the clones from Ebay. There is example code for the Arduino available from the Sparkfun site in https://learn.sparkfun.com/tutorials/graphic-lcd-hookup-guide This is a 3.3V device, if you are running it from a 5V micro you need a 5V tolorant level translator such as the 74ahc367 to protect the signal imputs. Rafa G. did a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
  ESP32 DOIT DEVKIT V1 36pin: ESP32 DOIT DEVKIT V1 36pin.
